// Logisim project CPU.circ as structural Verilog: 6 circuits, main circuit Processor
module Processor (
);

  wire ALU_EQ, ALU_LT, ALU_LTU, ALU_RDY, and_1_out, and_2_out, and_3_out, and_4_out, and_5_out, and_6_out,
       BREAK, button_1_out, button_2_out, button_3_out, CLK, EALIGN, FETCH, INT, JMP, LDSX, LINK, LOAD0,
       LOAD1, loadstoreunit_1_bm0, loadstoreunit_1_bm1, loadstoreunit_1_bm2, loadstoreunit_1_bm3,
       loadstoreunit_1_ealign, loadstoreunit_1_nrw, loadstoreunit_1_strobe, multiplexer_5_out, not_1_out,
       not_2_out, not_3_out, OPIMM, or_1_out, PCE, PCREL, programcounter_1_ealign, REG_WE, RST, SIGILL, SLT,
       SLTU, STEP, STORE0, STORE1, SYSTEM;
  wire [3:0] ALU_OP;
  wire [4:0] WI, XI, YI;
  wire [15:0] loadstoreunit_1_a;
  wire [29:16] loadstoreunit_1_a_2;
  wire [31:0] ALU_R, bit_extender_1_out, IMM, INSTR, LSU_IN, multiplexer_1_out, multiplexer_2_out,
       multiplexer_3_out, multiplexer_4_out, MUX_R, PC, PPC, ram_1_data, REG_X, REG_Y, register_1_q,
       rom_1_data, SPC;

  and and_1 (and_1_out, 1'b1, loadstoreunit_1_a_2[29], loadstoreunit_1_a_2[28], loadstoreunit_1_a_2[27], loadstoreunit_1_a_2[26], loadstoreunit_1_a_2[25], loadstoreunit_1_a_2[24], loadstoreunit_1_a_2[23], loadstoreunit_1_a_2[22], loadstoreunit_1_a_2[21], loadstoreunit_1_a_2[20], loadstoreunit_1_a_2[19], loadstoreunit_1_a_2[18], loadstoreunit_1_a_2[17], loadstoreunit_1_a_2[16]);
  not not_1 (not_1_out, and_1_out);
  not not_2 (not_2_out, not_3_out);
  ROM #(.addrWidth(16), .dataWidth(32)) rom_1 (.addr(loadstoreunit_1_a), .data(rom_1_data));
  RAM #(.addrWidth(16), .asyncread("true"), .byteenables("byteEnables"), .dataWidth(32), .databus("bidir")) ram_1 (
    .addr(loadstoreunit_1_a), .we(and_2_out), .oe(and_3_out), .clk(loadstoreunit_1_strobe),
    .data(ram_1_data), .be3(loadstoreunit_1_bm3), .be2(loadstoreunit_1_bm2), .be1(loadstoreunit_1_bm1),
    .be0(loadstoreunit_1_bm0));
  and and_2 (and_2_out, not_2_out, not_1_out);
  and and_3 (and_3_out, not_1_out, not_3_out);
  Button button_1 (.out(button_1_out));
  Button button_2 (.out(button_2_out));
  Button button_3 (.out(button_3_out));
  Clock clock_1 (.out(CLK));
  T_Flip_Flop t_ff_1 (.T(1'b1), .clk(button_1_out), .Q(RST));  // open: Qn, reset, preset
  T_Flip_Flop t_ff_2 (.T(1'b1), .clk(button_2_out), .Q(INT));  // open: Qn, reset, preset
  T_Flip_Flop t_ff_3 (.T(1'b1), .clk(button_3_out), .Q(FETCH));  // open: Qn, reset, preset
  Register #(.width(32)) register_1 (.D(rom_1_data), .clk(and_4_out), .Q(register_1_q));  // open: en, clr
  and and_4 (and_4_out, and_1_out, loadstoreunit_1_strobe);
  // Probe on {loadstoreunit_1_a_2, loadstoreunit_1_a}
  // Probe on ram_1_data
  assign ram_1_data = and_5_out ? register_1_q : 32'bz;  // Controlled_Buffer controlled_buffer_1
  and and_5 (and_5_out, and_1_out, not_3_out);
  or or_1 (or_1_out, LOAD1, LOAD0);
  Multiplexer #(.width(32)) multiplexer_1 (.in0(MUX_R), .in1(LSU_IN), .out(multiplexer_1_out), .sel(or_1_out));
  not not_3 (not_3_out, loadstoreunit_1_nrw);
  // Probe on multiplexer_2_out
  RegisterFile registerfile_1 (.Y(REG_Y), .X(REG_X), .YI(YI), .D(multiplexer_2_out), .WI(WI), .WR(and_6_out), .XI(XI));
  Multiplexer #(.width(32)) multiplexer_2 (.in0(multiplexer_1_out), .in1(SPC), .out(multiplexer_2_out), .sel(LINK));
  and and_6 (and_6_out, REG_WE, CLK);
  LoadStoreUnit loadstoreunit_1 (
    .DO(ram_1_data), .INSTR(INSTR), .DIN(LSU_IN), .PCE(PCE), .A({loadstoreunit_1_a_2, loadstoreunit_1_a}),
    .STROBE(loadstoreunit_1_strobe), .EALIGN(loadstoreunit_1_ealign), .BM0(loadstoreunit_1_bm0),
    .BM1(loadstoreunit_1_bm1), .BM2(loadstoreunit_1_bm2), .BM3(loadstoreunit_1_bm3),
    .nRW(loadstoreunit_1_nrw), .LDSX(LDSX), .STEP(STEP), .FETCH(FETCH), .nBUSY(1'b1), .CLK(CLK), .RST(RST),
    .LOAD0(LOAD0), .LOAD1(LOAD1), .STORE0(STORE0), .STORE1(STORE1), .ADDR(ALU_R), .PC(PC), .DI(ram_1_data),
    .DOUT(REG_Y));  // open: RDY
  ProgramCounter programcounter_1 (
    .EALIGN(programcounter_1_ealign), .PC(PC), .SPC(SPC), .PPC(PPC), .CLK(CLK), .ADDR(MUX_R), .RST(RST),
    .INT(INT), .JMP(JMP), .PCE(PCE));
  or or_2 (EALIGN, loadstoreunit_1_ealign, programcounter_1_ealign);
  // Probe on PPC
  Multiplexer #(.width(32)) multiplexer_3 (.in0(REG_X), .in1(PPC), .out(multiplexer_3_out), .sel(PCREL));
  Multiplexer #(.width(32)) multiplexer_4 (.in0(REG_Y), .in1(IMM), .out(multiplexer_4_out), .sel(OPIMM));
  InstructionDecoder instructiondecoder_1 (
    .SYSTEM(SYSTEM), .SIGILL(SIGILL), .BREAK(BREAK), .IMM(IMM), .STEP(STEP), .WI(WI), .XI(XI), .YI(YI),
    .PCREL(PCREL), .OPIMM(OPIMM), .REG_WE(REG_WE), .LINK(LINK), .SLT(SLT), .SLTU(SLTU), .LDSX(LDSX),
    .LOAD0(LOAD0), .LOAD1(LOAD1), .STORE0(STORE0), .STORE1(STORE1), .ALU_OP(ALU_OP), .JMP(JMP), .CLK(CLK),
    .EQ(ALU_EQ), .LT(ALU_LT), .LTU(ALU_LTU), .INSTR(INSTR));
  ArithmeticLogicUnit arithmeticlogicunit_1 (
    .R(ALU_R), .RDY(ALU_RDY), .EQ(ALU_EQ), .LT(ALU_LT), .LTU(ALU_LTU), .SEL(ALU_OP), .X(multiplexer_3_out),
    .Y(multiplexer_4_out), .CLK(CLK));
  // Probe on multiplexer_3_out
  // Probe on multiplexer_4_out
  assign bit_extender_1_out = {{31{multiplexer_5_out}}, multiplexer_5_out};  // Bit_Extender bit_extender_1
  Multiplexer multiplexer_5 (.in0(ALU_LT), .in1(ALU_LTU), .out(multiplexer_5_out), .sel(SLTU));
  Multiplexer #(.width(32)) multiplexer_6 (.in0(ALU_R), .in1(bit_extender_1_out), .out(MUX_R), .sel(SLT));
  // Probe on MUX_R
  LED led_1 (.in(SIGILL));
  // Probe on IMM
  // Probe on WI
  // Probe on XI
  // Probe on YI

  // Notes on the sheet:
  //   contents of rom_1 (hex, n*v repeats v):
  //   1300613 100793 100713 f706b3 fed66ae3 78713 68793 ff1ff06f 65524*0 10000113 fffc00b7 8067
endmodule

module RegisterFile (
  input  [4:0] WI,
  input  WR,
  input  [31:0] D,
  input  [4:0] XI,
  input  [4:0] YI,
  output [31:0] X,
  output [31:0] Y
);

  wire W1, W2, W3, W4, W5, W6, W7, W8, W9, W10, W11, W12, W13, W14, W15, W16, W17, W18, W19, W20, W21, W22,
       W23, W24, W25, W26, W27, W28, W29, W30, W31;
  wire [0:0] decoder_1_out0;
  wire [31:0] R1, R2, R3, R4, R5, R6, R7, R8, R9, R10, R11, R12, R13, R14, R15, R16, R17, R18, R19, R20, R21,
       R22, R23, R24, R25, R26, R27, R28, R29, R30, R31;

  Register #(.width(32)) register_1 (.D(D), .clk(W1), .Q(R1));  // open: en, clr
  Register #(.width(32)) register_2 (.D(D), .clk(W2), .Q(R2));  // open: en, clr
  Register #(.width(32)) register_3 (.D(D), .clk(W3), .Q(R3));  // open: en, clr
  // NoConnect on decoder_1_out0[0]
  Register #(.width(32)) register_4 (.D(D), .clk(W4), .Q(R4));  // open: en, clr
  Register #(.width(32)) register_5 (.D(D), .clk(W5), .Q(R5));  // open: en, clr
  Register #(.width(32)) register_6 (.D(D), .clk(W6), .Q(R6));  // open: en, clr
  Register #(.width(32)) register_7 (.D(D), .clk(W7), .Q(R7));  // open: en, clr
  Decoder #(.select(5)) decoder_1 (
    .out0(decoder_1_out0[0]), .out1(W1), .out2(W2), .out3(W3), .out4(W4), .out5(W5), .out6(W6), .out7(W7),
    .out8(W8), .out9(W9), .out10(W10), .out11(W11), .out12(W12), .out13(W13), .out14(W14), .out15(W15),
    .out16(W16), .out17(W17), .out18(W18), .out19(W19), .out20(W20), .out21(W21), .out22(W22), .out23(W23),
    .out24(W24), .out25(W25), .out26(W26), .out27(W27), .out28(W28), .out29(W29), .out30(W30), .out31(W31),
    .sel(WI), .en(WR));
  Register #(.width(32)) register_8 (.D(D), .clk(W8), .Q(R8));  // open: en, clr
  Register #(.width(32)) register_9 (.D(D), .clk(W9), .Q(R9));  // open: en, clr
  Register #(.width(32)) register_10 (.D(D), .clk(W10), .Q(R10));  // open: en, clr
  Register #(.width(32)) register_11 (.D(D), .clk(W11), .Q(R11));  // open: en, clr
  Register #(.width(32)) register_12 (.D(D), .clk(W12), .Q(R12));  // open: en, clr
  Register #(.width(32)) register_13 (.D(D), .clk(W13), .Q(R13));  // open: en, clr
  Register #(.width(32)) register_14 (.D(D), .clk(W14), .Q(R14));  // open: en, clr
  Register #(.width(32)) register_15 (.D(D), .clk(W15), .Q(R15));  // open: en, clr
  Multiplexer #(.select(5), .width(32)) multiplexer_1 (
    .in0({32{1'b0}}), .in1(R1), .in2(R2), .in3(R3), .in4(R4), .in5(R5), .in6(R6), .in7(R7), .in8(R8),
    .in9(R9), .in10(R10), .in11(R11), .in12(R12), .in13(R13), .in14(R14), .in15(R15), .in16(R16), .in17(R17),
    .in18(R18), .in19(R19), .in20(R20), .in21(R21), .in22(R22), .in23(R23), .in24(R24), .in25(R25),
    .in26(R26), .in27(R27), .in28(R28), .in29(R29), .in30(R30), .in31(R31), .out(X), .sel(XI));
  Register #(.width(32)) register_16 (.D(D), .clk(W16), .Q(R16));  // open: en, clr
  Register #(.width(32)) register_17 (.D(D), .clk(W17), .Q(R17));  // open: en, clr
  Register #(.width(32)) register_18 (.D(D), .clk(W18), .Q(R18));  // open: en, clr
  Register #(.width(32)) register_19 (.D(D), .clk(W19), .Q(R19));  // open: en, clr
  Register #(.width(32)) register_20 (.D(D), .clk(W20), .Q(R20));  // open: en, clr
  Register #(.width(32)) register_21 (.D(D), .clk(W21), .Q(R21));  // open: en, clr
  Register #(.width(32)) register_22 (.D(D), .clk(W22), .Q(R22));  // open: en, clr
  Register #(.width(32)) register_23 (.D(D), .clk(W23), .Q(R23));  // open: en, clr
  Register #(.width(32)) register_24 (.D(D), .clk(W24), .Q(R24));  // open: en, clr
  Register #(.width(32)) register_25 (.D(D), .clk(W25), .Q(R25));  // open: en, clr
  Register #(.width(32)) register_26 (.D(D), .clk(W26), .Q(R26));  // open: en, clr
  Register #(.width(32)) register_27 (.D(D), .clk(W27), .Q(R27));  // open: en, clr
  Multiplexer #(.select(5), .width(32)) multiplexer_2 (
    .in0({32{1'b0}}), .in1(R1), .in2(R2), .in3(R3), .in4(R4), .in5(R5), .in6(R6), .in7(R7), .in8(R8),
    .in9(R9), .in10(R10), .in11(R11), .in12(R12), .in13(R13), .in14(R14), .in15(R15), .in16(R16), .in17(R17),
    .in18(R18), .in19(R19), .in20(R20), .in21(R21), .in22(R22), .in23(R23), .in24(R24), .in25(R25),
    .in26(R26), .in27(R27), .in28(R28), .in29(R29), .in30(R30), .in31(R31), .out(Y), .sel(YI));
  Register #(.width(32)) register_28 (.D(D), .clk(W28), .Q(R28));  // open: en, clr
  Register #(.width(32)) register_29 (.D(D), .clk(W29), .Q(R29));  // open: en, clr
  Register #(.width(32)) register_30 (.D(D), .clk(W30), .Q(R30));  // open: en, clr
  Register #(.width(32)) register_31 (.D(D), .clk(W31), .Q(R31));  // open: en, clr

  // Other names for the same wires on the sheet: DI[31:0] = D
endmodule

module ProgramCounter (
  input  [31:0] ADDR,
  input  RST,
  input  INT,
  input  JMP,
  input  PCE,
  input  CLK,
  output [31:0] PC,
  output [31:0] SPC,
  output [31:0] PPC,
  output EALIGN
);

  wire and_1_out, n74161_1_pin1, n74161_1_pin5, n74161_1_pin6, n74161_1_pin7, n74161_1_pin9, n74161_1_pin10,
       n74161_2_pin7, n74161_2_pin10, n74161_3_pin1, n74161_3_pin7, n74161_3_pin10, n74161_4_pin1,
       n74161_4_pin7, n74161_4_pin10, n74161_5_pin1, n74161_5_pin7, n74161_5_pin10, n74161_6_pin1,
       n74161_6_pin7, n74161_6_pin10, n74161_7_pin1, n74161_7_pin7, n74161_7_pin10, n74161_8_pin1,
       n74161_8_pin7, not_1_out, or_1_out;
  wire [3:0] n74161_6_pin3;
  wire [29:0] multiplexer_1_out;

  _74161 #(.ShowInternalStructure("true")) u_74161_1 (
    .pin1(n74161_1_pin1), .pin2(CLK), .pin3(multiplexer_1_out[28]), .pin4(multiplexer_1_out[29]),
    .pin5(n74161_1_pin5), .pin6(n74161_1_pin6), .pin7(n74161_1_pin7), .pin14(PC[31]), .pin13(PC[30]),
    .pin10(n74161_1_pin10), .pin9(n74161_1_pin9));  // open: pin15, pin12, pin11
  _74161 #(.ShowInternalStructure("true")) u_74161_2 (
    .pin2(CLK), .pin3(multiplexer_1_out[24]), .pin4(multiplexer_1_out[25]), .pin5(multiplexer_1_out[26]),
    .pin6(multiplexer_1_out[27]), .pin7(n74161_2_pin7), .pin15(n74161_1_pin10), .pin14(PC[26]),
    .pin13(PC[27]), .pin12(PC[28]), .pin11(PC[29]), .pin10(n74161_2_pin10), .pin9(n74161_1_pin9));  // open: pin1
  _74161 #(.ShowInternalStructure("true")) u_74161_3 (
    .pin1(n74161_3_pin1), .pin2(CLK), .pin3(multiplexer_1_out[20]), .pin4(multiplexer_1_out[21]),
    .pin5(multiplexer_1_out[22]), .pin6(multiplexer_1_out[23]), .pin7(n74161_3_pin7), .pin15(n74161_2_pin10),
    .pin14(PC[22]), .pin13(PC[23]), .pin12(PC[24]), .pin11(PC[25]), .pin10(n74161_3_pin10),
    .pin9(n74161_1_pin9));
  _74161 #(.ShowInternalStructure("true")) u_74161_4 (
    .pin1(n74161_4_pin1), .pin2(CLK), .pin3(multiplexer_1_out[16]), .pin4(multiplexer_1_out[17]),
    .pin5(multiplexer_1_out[18]), .pin6(multiplexer_1_out[19]), .pin7(n74161_4_pin7), .pin15(n74161_3_pin10),
    .pin14(PC[18]), .pin13(PC[19]), .pin12(PC[20]), .pin11(PC[21]), .pin10(n74161_4_pin10),
    .pin9(n74161_1_pin9));
  _74161 #(.ShowInternalStructure("true")) u_74161_5 (
    .pin1(n74161_5_pin1), .pin2(CLK), .pin3(multiplexer_1_out[12]), .pin4(multiplexer_1_out[13]),
    .pin5(multiplexer_1_out[14]), .pin6(multiplexer_1_out[15]), .pin7(n74161_5_pin7), .pin15(n74161_4_pin10),
    .pin14(PC[14]), .pin13(PC[15]), .pin12(PC[16]), .pin11(PC[17]), .pin10(n74161_5_pin10),
    .pin9(n74161_1_pin9));
  _74161 #(.ShowInternalStructure("true")) u_74161_6 (
    .pin1(n74161_6_pin1), .pin2(CLK), .pin3(n74161_6_pin3[0]), .pin4(n74161_6_pin3[1]),
    .pin5(n74161_6_pin3[2]), .pin6(n74161_6_pin3[3]), .pin7(n74161_6_pin7), .pin15(n74161_5_pin10),
    .pin14(PC[10]), .pin13(PC[11]), .pin12(PC[12]), .pin11(PC[13]), .pin10(n74161_6_pin10),
    .pin9(n74161_1_pin9));
  _74161 #(.ShowInternalStructure("true")) u_74161_7 (
    .pin1(n74161_7_pin1), .pin2(CLK), .pin3(multiplexer_1_out[4]), .pin4(multiplexer_1_out[5]),
    .pin5(multiplexer_1_out[6]), .pin6(multiplexer_1_out[7]), .pin7(n74161_7_pin7), .pin15(n74161_6_pin10),
    .pin14(PC[6]), .pin13(PC[7]), .pin12(PC[8]), .pin11(PC[9]), .pin10(n74161_7_pin10), .pin9(n74161_1_pin9));
  Multiplexer #(.width(30)) multiplexer_1 (
    .in0(ADDR[31:2]), .in1(30'h3ffffffc),
    .out({multiplexer_1_out[29:12], n74161_6_pin3, multiplexer_1_out[7:0]}), .sel(or_1_out));
  Register #(.trigger("high"), .width(32)) register_1 (.D({PC[31:2], 2'b00}), .clk(1'b1));  // open: en, Q, clr
  or or_1 (or_1_out, INT, RST);
  Register #(.width(32)) register_2 (.D({PC[31:2], 2'b00}), .clk(not_1_out), .Q(SPC));  // open: en, clr
  not not_1 (not_1_out, CLK);
  _74161 #(.ShowInternalStructure("true")) u_74161_8 (
    .pin1(n74161_8_pin1), .pin2(CLK), .pin3(multiplexer_1_out[0]), .pin4(multiplexer_1_out[1]),
    .pin5(multiplexer_1_out[2]), .pin6(multiplexer_1_out[3]), .pin7(n74161_8_pin7), .pin15(n74161_7_pin10),
    .pin14(PC[2]), .pin13(PC[3]), .pin12(PC[4]), .pin11(PC[5]), .pin10(PCE), .pin9(n74161_1_pin9));
  or or_2 (EALIGN, ADDR[1], ADDR[0]);
  and and_1 (and_1_out, CLK, PCE);
  Register #(.width(32)) register_3 (.D(SPC), .clk(and_1_out), .Q(PPC));  // open: en, clr
  nor nor_1 (n74161_1_pin9, RST, INT, JMP);

  assign PC[1:0] = 2'b00;
  // also tied to GND on the sheet: {n74161_1_pin5, n74161_1_pin6}
  // also tied to VCC on the sheet: {n74161_1_pin1, n74161_1_pin7, n74161_2_pin7, n74161_3_pin1, n74161_3_pin7, n74161_4_pin1, n74161_4_pin7, n74161_5_pin1, n74161_5_pin7, n74161_6_pin1, n74161_6_pin7, n74161_7_pin1, n74161_7_pin7, n74161_8_pin1, n74161_8_pin7}
endmodule

module InstructionDecoder (
  input  [31:0] INSTR,
  input  CLK,
  input  EQ,
  input  LT,
  input  LTU,
  output STEP,
  output SIGILL,
  output JMP,
  output PCREL,
  output OPIMM,
  output REG_WE,
  output LINK,
  output SLT,
  output SLTU,
  output LDSX,
  output LOAD0,
  output [31:0] IMM,
  output LOAD1,
  output STORE0,
  output STORE1,
  output [3:0] ALU_OP,
  output SYSTEM,
  output [4:0] WI,
  output [4:0] XI,
  output [4:0] YI,
  output BREAK
);

  wire and_6_out, and_7_out, decoder_1_out0, decoder_1_out1, decoder_1_out2, decoder_1_out3,
       multiplexer_1_out, multiplexer_2_out, nand_1_out, nand_2_out, not_1_out, nSHIFT, or_2_out, or_3_out,
       P7, P30, P31, RD, RS1, RS2, S4_1_0, S4_1_1, S10_5, S19_12, S30_20, SIGILL_t;
  wire [0:0] IDEC_p3;
  wire [1:0] register_1_q, StageCounter_q;
  wire [2:0] and_4_out, FUNCT3, register_2_q;
  wire [3:0] and_8_out, and_9_out, P11_8;
  wire [4:0] OP, P30_25;
  wire [4:1] P24_20;
  wire [5:5] and_5_out;
  wire [7:3] P19_12;
  wire [8:3] CLF_p3;
  wire [9:9] xor_1_out;
  wire [20:17] MicroCode_data;

  Register #(.width(32)) register_1 (
    .D(INSTR), .clk(nand_1_out),
    .Q({P31, P30, P30_25, P24_20, BREAK, P19_12, FUNCT3, P11_8, P7, OP, register_1_q}));  // open: en, clr
  nand nand_1 (nand_1_out, STEP, CLK);
  Register #(.width(3)) register_2 (.D({LTU, LT, EQ}), .clk(CLK), .Q(register_2_q));  // open: en, clr
  Counter #(.max('h3), .width(2)) StageCounter (
    .load(STEP), .clk(not_1_out), .D(2'b00), .Q(StageCounter_q));  // open: clr, up, count, carry
  not not_1 (not_1_out, CLK);
  Multiplexer multiplexer_1 (.in0(register_2_q[1]), .in1(register_2_q[2]), .out(multiplexer_1_out), .sel(FUNCT3[1]));
  Multiplexer multiplexer_2 (.in0(register_2_q[0]), .in1(multiplexer_1_out), .out(multiplexer_2_out), .sel(FUNCT3[2]));
  LED COND (.in(xor_1_out[9]));
  LED S0 (.in(decoder_1_out0));
  LED S1 (.in(decoder_1_out1));
  LED S2 (.in(decoder_1_out2));
  LED S3 (.in(decoder_1_out3));
  nand nand_2 (nand_2_out, register_1_q[0], register_1_q[1]);
  // Probe on OP
  assign WI = {5{RD}} & {P11_8, P7};  // AND_Gate and_1, 5 bits wide
  // Probe on {P11_8, P7}
  // Probe on FUNCT3
  assign XI = {5{RS1}} & P19_12;  // AND_Gate and_2, 5 bits wide
  // Probe on P19_12
  assign YI = {5{RS2}} & {P24_20, BREAK};  // AND_Gate and_3, 5 bits wide
  // Probe on {P24_20, BREAK}
  // Probe on {P31, P30, P30_25}
  ROM #(.addrWidth(12), .dataWidth(21)) MicroCode (
    .addr({StageCounter_q, xor_1_out[9], P30, and_4_out, OP}),
    .data({MicroCode_data[20], SYSTEM, nSHIFT, MicroCode_data[17], ALU_OP, STORE1, STORE0, LOAD1, LOAD0, LDSX, SLTU, SLT, LINK, REG_WE, OPIMM, PCREL, JMP, STEP}));
  assign and_4_out = {3{RS1}} & FUNCT3;  // AND_Gate and_4, 3 bits wide
  xor xor_1 (xor_1_out[9], FUNCT3[0], multiplexer_2_out);
  Decoder #(.enable("false"), .select(2)) decoder_1 (
    .out0(decoder_1_out0), .out1(decoder_1_out1), .out2(decoder_1_out2), .out3(decoder_1_out3),
    .sel(StageCounter_q));
  // PlaRom #(.Contents("1 2 2 1 1 2 2 1 1 2*4 1*4 0 1*5 2 2 1 2 1*3 2 2 1*4 0 2 1 2*3 1 2 2 0 2 0 1*3 0 0 1 1 2 2 1 1 0 0 2 1*4 2 0 1*3 0 2 1 0 2 2 1 0 2 0 2 2 1 1 1 0*9 1 0*8 1 0*8 1 0*6 1 0 1 0*4 1 0 1 0 0 1 0*9 1 0*9 1 0*9 1 0*9 1 0*8 1 0*8 1 0*9 1 0*8 1 0*9 1 0*8 1 0*8 1"), .\and (17), .outputs(9)) CLF: pin names not known; wires that end beside it: OP, 1'b0, {CLF_p3, RS1, RS2, RD}
  LED R (.in(CLF_p3[8]));
  LED I (.in(CLF_p3[7]));
  LED S (.in(CLF_p3[6]));
  LED B (.in(CLF_p3[5]));
  LED U (.in(CLF_p3[4]));
  LED J (.in(CLF_p3[3]));
  // PlaRom #(.Contents("0 0 2 1 2 1*3 0 2 0 2*3 1 1 0 2 0 2 2 1 1 2 0 2 0 1*3 2 2 0 2 0 1 1 0 1 1 0*3 2*3 1 1 0*3 2 2 1 0 2 0*3 1*3 2 2 0*3 1 1 0 1 1 0*4 2 1*3 0*3 2 0*8 1 0 0 1 0*5 1 0*8 2 0*3 2*3 1*3 0 2 0 2 2 1 2*3 0 0 2 0*4 2 0*3 1 0 0 1 2 0*4 1 0 0 2 0*5 2 0*4 1 0 2 1 2 0*3 2 2 1 2*3 0*3 1 0*3 2 0*6 2 0*3 2 1 0*6 2 0 2 0 2 0*3 1 2 1 0 2 0*3 1 0 1 1 2 0*5 2 2 0*7 2 1 1 0*8 1 0*8 1 0*8 1 0*8 1 0*9 1 0*8 1 0*8 1 0*8 1 0*9 1 0*9 1 0*8 1 0*8 1 0*8 1 0*9 1 0*8 1 0*8 1 0 0 1 0*5 1 0*8 1 0 0 1 0*5 1 0 0 1 0*6 1 1 0*7 1 0*10 1 0*8 1 0*9 1 0*8 1 0*8 1 0*8 1 0*8 1 0*8 1"), .\and (30), .outputs(9)) IDEC: pin names not known; wires that end beside it: {P31, BREAK, P7, OP}, 1'b0, {IMM[0], S4_1_0, S4_1_1, S10_5, IMM[11], S19_12, S30_20, IMM[31], IDEC_p3[0]}
  or or_1 (SIGILL, nand_2_out, SIGILL_t, IDEC_p3[0]);
  or or_2 (or_2_out, P31, P30_25[4], P30_25[3], P30_25[2], P30_25[1], P30_25[0]);
  or or_3 (or_3_out, P24_20[4], P24_20[3], P24_20[2], P24_20[1]);
  and and_5 (and_5_out[5], S10_5, nSHIFT);
  and and_6 (and_6_out, or_2_out, MicroCode_data[17]);
  or or_4 (SIGILL_t, and_6_out, MicroCode_data[20], and_7_out);
  and and_7 (and_7_out, SYSTEM, or_3_out);
  assign and_8_out = {4{S4_1_1}} & P11_8;  // AND_Gate and_8, 4 bits wide
  assign and_9_out = {4{S4_1_0}} & P24_20;  // AND_Gate and_9, 4 bits wide
  Multiplexer #(.width(8)) multiplexer_3 (.in0({8{IMM[31]}}), .in1({P19_12, FUNCT3}), .out(IMM[19:12]), .sel(S19_12));
  Multiplexer #(.width(11)) multiplexer_4 (
    .in0({11{IMM[31]}}), .in1({P30, P30_25, P24_20, BREAK}), .out(IMM[30:20]), .sel(S30_20));
  assign IMM[4:1] = and_8_out | and_9_out;  // OR_Gate or_5, 4 bits wide
  assign IMM[10:5] = {6{and_5_out[5]}} & {P30, P30_25};  // AND_Gate and_10, 6 bits wide

  // Other names for the same wires on the sheet: P20 = BREAK; P24_20[0] = BREAK; P24_21[3:0] = P24_20;
  //   P30_25[5] = P30; X0 = IMM[0]; X11 = IMM[11]; X31 = IMM[31]; P19_12[2:0] = FUNCT3

  // Notes on the sheet:
  //   2'b11
  //   OP
  //   rd/imm
  //   funct3/imm
  //   rs1/imm
  //   rs2/imm
  //   funct7/imm
  //   contents of MicroCode (hex, n*v repeats v):
  //   40311 140001 140001 40001 40019 40015 140001 140001 40809 140001 140001 140001 60011 40019 10*140001
  //   40000 4003a 140001 4003e e0001 140001 140001 140001 40511 140001 140001 140001 3a019 140001 140001
  //   140001 41009 140001 140001 140001 7a011 11*140001 40000 7*140001 40611 140001 140001 140001 40059
  //   140001 140001 140001 41809 140001 140001 140001 60051 23*140001 400d9 7*140001 600d1 19*140001 40211
  //   140001 140001 140001 58019 7*140001 78011 11*140001 40000 7*140001 40411 140001 140001 140001 3c019
  //   7*140001 7c011 11*140001 40000 11*140001 54019 7*140001 74011 11*140001 40000 11*140001 56019
  //   7*140001 76011 11*140001 40000 7*140001 40311 140001 140001 40001 40019 40015 140001 140001 40809
  //   140001 140001 140001 62011 40019 10*140001 40000 4003a 140001 4003e 4*140001 40511 7*140001 41009
  //   15*140001 40000 7*140001 40611 140001 140001 140001 40059 140001 140001 140001 41809 27*140001 400d9
  //   27*140001 40211 140001 140001 140001 58019 19*140001 40000 7*140001 40411 140001 140001 140001 3e019
  //   7*140001 7e011 11*140001 40000 11*140001 54019 19*140001 40000 11*140001 56019 19*140001 40000
  //   7*140001 40311 140001 140001 40001 40019 40015 140001 140001 40809 140001 140001 140001 60011 40019
  //   10*140001 40000 4003a 140001 4003e e0001 140001 140001 140001 40511 140001 140001 140001 3a019
  //   140001 140001 140001 41009 140001 140001 140001 7a011 11*140001 40000 7*140001 40611 140001 140001
  //   140001 40059 140001 140001 140001 41809 140001 140001 140001 60051 23*140001 400d9 7*140001 600d1
  //   19*140001 40211 140001 140001 140001 58019 7*140001 78011 11*140001 40000 7*140001 40411 140001
  //   140001 140001 3c019 7*140001 7c011 11*140001 40000 11*140001 54019 7*140001 74011 11*140001 40000
  //   11*140001 56019 7*140001 76011 11*140001 40000 7*140001 40311 140001 140001 40001 40019 40015 140001
  //   140001 40809 140001 140001 140001 62011 40019 10*140001 40000 4003a 140001 4003e 4*140001 40511
  //   7*140001 41009 15*140001 40000 7*140001 40611 140001 140001 140001 40059 140001 140001 140001 41809
  //   27*140001 400d9 27*140001 40211 140001 140001 140001 58019 19*140001 40000 7*140001 40411 140001
  //   140001 140001 3e019 7*140001 7e011 11*140001 40000 11*140001 54019 19*140001 40000 11*140001 56019
  //   19*140001 40000 31*140001 40001 40001 140001 40001 28*140001 40001 95*140001 40001 31*140001 40001
  //   31*140001 40001 31*140001 40001 31*140001 40001 40001 140001 40001 28*140001 40001 95*140001 40001
  //   31*140001 40001 31*140001 40001 31*140001 40001 31*140001 4000e 40001 140001 40001 28*140001 4000e
  //   95*140001 4000e 31*140001 4000e 31*140001 4000e 31*140001 4000e 31*140001 4000e 40001 140001 40001
  //   28*140001 4000e 95*140001 4000e 31*140001 4000e 31*140001 4000e 31*140001 4000e 31*140001 40001
  //   31*140001 40001 95*140001 40001 31*140001 40001 31*140001 40001 31*140001 40001 31*140001 40001
  //   31*140001 40001 95*140001 40001 31*140001 40001 31*140001 40001 31*140001 40001 31*140001 40001
  //   31*140001 40001 95*140001 40001 31*140001 40001 31*140001 40001 31*140001 40001 31*140001 40001
  //   31*140001 40001 95*140001 40001 31*140001 40001 31*140001 40001 31*140001 40001 1031*140001
  //   ILL
  //   X31
  //   S[30:20]
  //   S[19:12]
  //   X11
  //   S[10:5]
  //   S[4:1].1
  //   S[4:1].0
  //   X0
endmodule

module ArithmeticLogicUnit (
  input  CLK,
  input  [31:0] X,
  input  [31:0] Y,
  input  [3:0] SEL,
  output RDY,
  output EQ,
  output LT,
  output LTU,
  output [31:0] R
);

  wire decoder_1_out0, decoder_1_out1, decoder_1_out2, decoder_1_out3, decoder_1_out4, decoder_1_out5,
       decoder_1_out6, decoder_1_out7, decoder_1_out8, decoder_1_out9, decoder_1_out10, decoder_1_out11,
       decoder_1_out12, decoder_1_out13, decoder_1_out14, decoder_1_out15, OVF;
  wire [31:0] ANDV, DIFF, ORV, SARV, shifter_1_out, shifter_2_out, shifter_3_out, SHLV, SHRV, SPRODH, SPRODL,
       SQUOT, SREM, SUM, UPRODH, UPRODL, UQUOT, UREM, XORV;

  Adder #(.width(32)) adder_1 (.a(X), .b(Y), .out(SUM));  // open: cin, cout
  Subtractor #(.width(32)) subtractor_1 (.a(X), .b(Y), .out(DIFF));  // open: bin, bout
  Multiplier #(.mode("twosComplement"), .width(32)) multiplier_1 (
    .a(X), .b(Y), .out(SPRODL), .cout(SPRODH));  // open: cin
  Multiplier #(.width(32)) multiplier_2 (.a(X), .b(Y), .out(UPRODL), .cout(UPRODH));  // open: cin
  Divider #(.mode("twosComplement"), .width(32)) divider_1 (.a(X), .b(Y), .out(SQUOT), .rem(SREM));  // open: upper
  Divider #(.width(32)) divider_2 (.a(X), .b(Y), .out(UQUOT), .rem(UREM));  // open: upper
  Register #(.trigger("high"), .width(32)) u_SUM (.D(SUM), .clk(1'b1));  // open: en, Q, clr
  Register #(.trigger("high"), .width(32)) u_DIFF (.D(DIFF), .clk(1'b1));  // open: en, Q, clr
  Register #(.trigger("high"), .width(32)) u_SPRODL (.D(SPRODL), .clk(1'b1));  // open: en, Q, clr
  Register #(.trigger("high"), .width(32)) u_SPRODH (.D(SPRODH), .clk(1'b1));  // open: en, Q, clr
  Register #(.trigger("high"), .width(32)) u_UPRODL (.D(UPRODL), .clk(1'b1));  // open: en, Q, clr
  Register #(.trigger("high"), .width(32)) u_UPRODH (.D(UPRODH), .clk(1'b1));  // open: en, Q, clr
  Register #(.trigger("high"), .width(32)) u_SQUOT (.D(SQUOT), .clk(1'b1));  // open: en, Q, clr
  Register #(.trigger("high"), .width(32)) u_SREM (.D(SREM), .clk(1'b1));  // open: en, Q, clr
  Register #(.trigger("high"), .width(32)) u_UQUOT (.D(UQUOT), .clk(1'b1));  // open: en, Q, clr
  Register #(.trigger("high"), .width(32)) u_UREM (.D(UREM), .clk(1'b1));  // open: en, Q, clr
  assign ORV = X | Y;  // OR_Gate or_1, 32 bits wide
  assign ANDV = X & Y;  // AND_Gate and_1, 32 bits wide
  assign XORV = X ^ Y;  // XOR_Gate xor_1, 32 bits wide
  Shifter #(.width(32)) shifter_1 (.in(X), .\dist (Y[4:0]), .out(shifter_1_out));
  Shifter #(.shift("lr"), .width(32)) shifter_2 (.in(X), .\dist (Y[4:0]), .out(shifter_2_out));
  Shifter #(.shift("ar"), .width(32)) shifter_3 (.in(X), .\dist (Y[4:0]), .out(shifter_3_out));
  Comparator #(.width(32)) comparator_1 (.a(X), .b(Y), .eq(EQ), .lt(LT));  // open: gt
  Comparator #(.mode("unsigned"), .width(32)) comparator_2 (.a(X), .b(Y), .lt(LTU));  // open: gt, eq
  Multiplexer #(.width(32)) multiplexer_1 (.in0(shifter_1_out), .in1({32{1'b0}}), .out(SHLV), .sel(OVF));
  Multiplexer #(.width(32)) multiplexer_2 (.in0(shifter_2_out), .in1({32{1'b0}}), .out(SHRV), .sel(OVF));
  Multiplexer #(.width(32)) multiplexer_3 (.in0(shifter_3_out), .in1({32{1'b0}}), .out(SARV), .sel(OVF));
  Register #(.trigger("high"), .width(32)) u_ORV (.D(ORV), .clk(1'b1));  // open: en, Q, clr
  Register #(.trigger("high"), .width(32)) u_ANDV (.D(ANDV), .clk(1'b1));  // open: en, Q, clr
  Register #(.trigger("high"), .width(32)) u_XORV (.D(XORV), .clk(1'b1));  // open: en, Q, clr
  Register #(.trigger("high"), .width(32)) u_SHLV (.D(SHLV), .clk(1'b1));  // open: en, Q, clr
  Register #(.trigger("high"), .width(32)) u_SHRV (.D(SHRV), .clk(1'b1));  // open: en, Q, clr
  Register #(.trigger("high"), .width(32)) u_SARV (.D(SARV), .clk(1'b1));  // open: en, Q, clr
  LED F_SUM (.in(decoder_1_out0));
  LED F_DIFF (.in(decoder_1_out1));
  LED F_SPRODL (.in(decoder_1_out2));
  LED F_SPRODH (.in(decoder_1_out3));
  LED F_UPRODL (.in(decoder_1_out4));
  LED F_UPRODH (.in(decoder_1_out5));
  LED F_SQUOT (.in(decoder_1_out6));
  LED F_SREM (.in(decoder_1_out7));
  LED F_UQUOT (.in(decoder_1_out8));
  LED F_UREM (.in(decoder_1_out9));
  LED F_ORV (.in(decoder_1_out10));
  LED F_ANDV (.in(decoder_1_out11));
  LED F_XORV (.in(decoder_1_out12));
  LED F_SHLV (.in(decoder_1_out13));
  LED F_SHRV (.in(decoder_1_out14));
  LED F_SARV (.in(decoder_1_out15));
  Multiplexer #(.select(4), .width(32)) multiplexer_4 (
    .in0(SUM), .in1(DIFF), .in2(SPRODL), .in3(SPRODH), .in4(UPRODL), .in5(UPRODH), .in6(SQUOT), .in7(SREM),
    .in8(UQUOT), .in9(UREM), .in10(ORV), .in11(ANDV), .in12(XORV), .in13(SHLV), .in14(SHRV), .in15(SARV),
    .out(R), .sel(SEL));
  Decoder #(.select(4)) decoder_1 (
    .out0(decoder_1_out0), .out1(decoder_1_out1), .out2(decoder_1_out2), .out3(decoder_1_out3),
    .out4(decoder_1_out4), .out5(decoder_1_out5), .out6(decoder_1_out6), .out7(decoder_1_out7),
    .out8(decoder_1_out8), .out9(decoder_1_out9), .out10(decoder_1_out10), .out11(decoder_1_out11),
    .out12(decoder_1_out12), .out13(decoder_1_out13), .out14(decoder_1_out14), .out15(decoder_1_out15),
    .sel(SEL), .en(1'b1));
  LED C_EQ (.in(EQ));
  LED C_LT (.in(LT));
  LED C_LTU (.in(LTU));
  or or_2 (OVF, Y[5], Y[6], Y[7], Y[8], Y[9], Y[10], Y[11], Y[12], Y[13], Y[14], Y[15], Y[16], Y[17], Y[18], Y[19], Y[20], Y[21], Y[22], Y[23], Y[24], Y[25], Y[26], Y[27], Y[28], Y[29], Y[30], Y[31]);

  assign RDY = 1'b1;

  // Other names for the same wires on the sheet: Y4_0[4:0] = Y[4:0]
endmodule

module LoadStoreUnit (
  input  nBUSY,
  input  CLK,
  input  RST,
  input  STEP,
  input  [31:0] DOUT,
  input  FETCH,
  input  LOAD0,
  input  LOAD1,
  input  STORE0,
  input  [31:0] DI,
  input  STORE1,
  input  [31:0] ADDR,
  input  [31:0] PC,
  input  LDSX,
  output STROBE,
  output RDY,
  output [31:0] DO,
  output EALIGN,
  output BM0,
  output BM1,
  output BM2,
  output BM3,
  output [31:0] INSTR,
  output nRW,
  output [31:0] DIN,
  output PCE,
  output [29:0] A
);

  wire and_9_out, and_10_out, d_ff_1_q, IO, LB, nor_1_out, not_1_out, not_2_out, not_3_out, not_4_out,
       not_5_out, or_1_out, S0, S1, S2, S3;
  wire [0:0] and_11_out;
  wire [6:0] bit_extender_9_out;
  wire [7:0] and_1_out, and_2_out, and_3_out, and_4_out, and_5_out, and_6_out, and_7_out, and_8_out,
       bit_extender_1_out, bit_extender_2_out, bit_extender_3_out, bit_extender_4_out, bit_extender_5_out,
       bit_extender_6_out, bit_extender_7_out, bit_extender_8_out;
  wire [15:0] bit_extender_10_out;
  wire [31:0] controlled_buffer_1_out, multiplexer_5_out, shifter_1_out, shifter_2_out, shifter_3_out,
       shifter_4_out, shifter_5_out, shifter_6_out;
  wire [31:8] controlled_buffer_5_out;

  Register #(.trigger("high"), .width(32)) MDR (.D(DI), .clk(1'b1));  // open: en, Q, clr
  assign bit_extender_1_out = {{7{BM0}}, BM0};  // Bit_Extender bit_extender_1
  assign bit_extender_2_out = {{7{BM1}}, BM1};  // Bit_Extender bit_extender_2
  assign bit_extender_3_out = {{7{BM2}}, BM2};  // Bit_Extender bit_extender_3
  assign bit_extender_4_out = {{7{BM3}}, BM3};  // Bit_Extender bit_extender_4
  assign and_1_out = DI[7:0] & bit_extender_1_out;  // AND_Gate and_1, 8 bits wide
  assign and_2_out = DI[15:8] & bit_extender_2_out;  // AND_Gate and_2, 8 bits wide
  assign and_3_out = DI[23:16] & bit_extender_3_out;  // AND_Gate and_3, 8 bits wide
  assign and_4_out = DI[31:24] & bit_extender_4_out;  // AND_Gate and_4, 8 bits wide
  Shifter #(.shift("lr"), .width(32)) shifter_1 (
    .in({and_4_out, and_3_out, and_2_out, and_1_out}), .\dist (5'b01000), .out(shifter_1_out));
  Shifter #(.shift("lr"), .width(32)) shifter_2 (
    .in({and_4_out, and_3_out, and_2_out, and_1_out}), .\dist (5'b10000), .out(shifter_2_out));
  Shifter #(.shift("lr"), .width(32)) shifter_3 (
    .in({and_4_out, and_3_out, and_2_out, and_1_out}), .\dist (5'b11000), .out(shifter_3_out));
  assign controlled_buffer_1_out = S0 ? DOUT : 32'bz;  // Controlled_Buffer controlled_buffer_1
  assign controlled_buffer_1_out = S1 ? shifter_4_out : 32'bz;  // Controlled_Buffer controlled_buffer_2
  Shifter #(.width(32)) shifter_4 (.in(DOUT), .\dist (5'b01000), .out(shifter_4_out));
  assign controlled_buffer_1_out = S2 ? shifter_5_out : 32'bz;  // Controlled_Buffer controlled_buffer_3
  Shifter #(.width(32)) shifter_5 (.in(DOUT), .\dist (5'b10000), .out(shifter_5_out));
  assign controlled_buffer_1_out = S3 ? shifter_6_out : 32'bz;  // Controlled_Buffer controlled_buffer_4
  Shifter #(.width(32)) shifter_6 (.in(DOUT), .\dist (5'b11000), .out(shifter_6_out));
  assign {controlled_buffer_5_out, DIN[7:0]} = S0 ? {and_4_out, and_3_out, and_2_out, and_1_out} : 32'bz;  // Controlled_Buffer controlled_buffer_5
  assign {controlled_buffer_5_out, DIN[7:0]} = S1 ? shifter_1_out : 32'bz;  // Controlled_Buffer controlled_buffer_6
  assign {controlled_buffer_5_out, DIN[7:0]} = S2 ? shifter_2_out : 32'bz;  // Controlled_Buffer controlled_buffer_7
  assign {controlled_buffer_5_out, DIN[7:0]} = S3 ? shifter_3_out : 32'bz;  // Controlled_Buffer controlled_buffer_8
  assign and_5_out = controlled_buffer_1_out[7:0] & bit_extender_5_out;  // AND_Gate and_5, 8 bits wide
  assign bit_extender_5_out = {{7{BM0}}, BM0};  // Bit_Extender bit_extender_5
  assign and_6_out = controlled_buffer_1_out[15:8] & bit_extender_6_out;  // AND_Gate and_6, 8 bits wide
  assign bit_extender_6_out = {{7{BM1}}, BM1};  // Bit_Extender bit_extender_6
  assign and_7_out = controlled_buffer_1_out[23:16] & bit_extender_7_out;  // AND_Gate and_7, 8 bits wide
  assign bit_extender_7_out = {{7{BM2}}, BM2};  // Bit_Extender bit_extender_7
  assign and_8_out = controlled_buffer_1_out[31:24] & bit_extender_8_out;  // AND_Gate and_8, 8 bits wide
  assign bit_extender_8_out = {{7{BM3}}, BM3};  // Bit_Extender bit_extender_8
  assign bit_extender_9_out = {{6{DIN[7]}}, DIN[7]};  // Bit_Extender bit_extender_9
  Multiplexer multiplexer_1 (.in0(controlled_buffer_5_out[15]), .in1(DIN[7]), .out(DIN[15]), .sel(and_9_out));
  and and_9 (and_9_out, LDSX, LB);
  assign DO = nRW ? {and_8_out, and_7_out, and_6_out, and_5_out} : 32'bz;  // Controlled_Buffer controlled_buffer_9
  Multiplexer #(.width(7)) multiplexer_2 (
    .in0(controlled_buffer_5_out[14:8]), .in1(bit_extender_9_out), .out(DIN[14:8]), .sel(and_9_out));
  Multiplexer #(.width(16)) multiplexer_3 (
    .in0(controlled_buffer_5_out[31:16]), .in1(bit_extender_10_out), .out(DIN[31:16]), .sel(LDSX));
  assign bit_extender_10_out = {{15{DIN[15]}}, DIN[15]};  // Bit_Extender bit_extender_10
  not not_1 (not_1_out, RST);
  and and_10 (and_10_out, not_1_out, PCE);
  Multiplexer #(.width(32)) multiplexer_4 (.in0(32'h13), .in1(DIN), .out(INSTR), .sel(and_10_out));
  and and_11 (and_11_out[0], STEP, FETCH);
  D_Flip_Flop d_ff_1 (.D(not_2_out), .clk(CLK), .Q(d_ff_1_q), .Qn(RDY), .reset(RST));  // open: preset
  not not_2 (not_2_out, nBUSY);
  and and_12 (LB, not_3_out, LOAD0);
  not not_3 (not_3_out, LOAD1);
  not not_4 (not_4_out, STEP);
  nor nor_1 (nor_1_out, not_4_out, STORE0, LOAD0, STORE1, LOAD1);
  and and_13 (PCE, and_11_out[0], nor_1_out);
  Multiplexer #(.width(32)) multiplexer_5 (.in0(ADDR), .in1(PC), .out(multiplexer_5_out), .sel(nor_1_out));
  not not_5 (not_5_out, RST);
  // PlaRom #(.Contents("0*6 2 0*5 2 0*5 2 0*5 2 0*5 2 0*4 1 1 0 0 2 2 0 1 1 2 0 0 2 0 1 1 0 2 2 0 0 1 1 2 2 0*3 2 2 1 0 1 2 0 2 2 1 2 1 0 0 2 1 0 1 2 1 0 2 1 2 1 0 1 0 1*6 2 2 1 1 0 1 2 0 2 1 1 2 1 0 0 1 1 0 0 2 0 0 1 1 2 0*4 1 2 1 0 1 2 0 1 2 1 2 1 0 0 1 1 0 1 0 1 2 1 1 0*4 2 1 1 0*3 2 0 1 1 0 2 0*4 2 0 0 2 0*3 2 2 0*4 2 0*3 2 2 0 2 0 2 0 0 2 0 2 0 0 2 2 0 0 2 0 2 2 0*4 2 0 1 0 1 2 2 0 1*4 2 1 0*6 1 0*6 1 0*6 1 1 0*5 1 1 0*7 1 1 0*5 1 1 0*5 1 1 0*5 1 1 0*5 1 0*6 1 0*6 1 1 0*5 1 1 0*5 1 1 0*6 1 0*6 1 0*7 1 1 0*5 1 1 0*5 1 0*6 1 0*6 1 0*7 1 0*6 1 0*6 1 0*7 1 0*6 1 0*6 1 0*6 1 0*6 1 0*6 1 0*6 1 0*6 1"), .\and (32), .outputs(7)) MaskGen: pin names not known; wires that end beside it: {multiplexer_5_out[1:0], STORE1, STORE0, LOAD1, LOAD0, and_11_out[0]}, 1'b0, {IO, nRW, BM3, BM2, BM1, BM0, EALIGN}
  Register #(.trigger("high"), .width(32)) MAR (.D(multiplexer_5_out), .clk(1'b1));  // open: en, Q, clr
  or or_1 (or_1_out, CLK, d_ff_1_q);
  and and_14 (STROBE, IO, or_1_out, not_5_out);
  Decoder #(.enable("false"), .select(2)) decoder_1 (
    .out0(S0), .out1(S1), .out2(S2), .out3(S3), .sel(multiplexer_5_out[1:0]));
  assign A = IO ? multiplexer_5_out[31:2] : 30'bz;  // Controlled_Buffer controlled_buffer_10

  // Other names for the same wires on the sheet: M0 = BM0; M1 = BM1; M2 = BM2; M3 = BM3; ST = nRW

  // Notes on the sheet:
  //   nBUSY: pull=up
  //   RST: pull=up
endmodule
